# Fritzing sketch breadboard (saved by Fritzing 0.8.7b)
breadboards: 1

parts:
  Bauteil1 = Arduino Uno (Rev3)
  LED1 = LED - 5mm [color="Red (633nm)" package="5 mm [THT]"]
  LED2 = LED - 5mm [color="Red (633nm)" package="5 mm [THT]"]
  LED3 = LED - 5mm [color="Red (633nm)" package="5 mm [THT]"]
  LED4 = LED - 5mm [color="Red (633nm)" package="5 mm [THT]"]
  R1 = Resistor [tolerance=±5% resistance=220 package=THT]
  R2 = Resistor [tolerance=±5% resistance=220 package=THT]

nets:
  N1: Bauteil1.D10_PWM/SS, R2.Pin_1
  N2: Bauteil1.D11_PWM/MOSI, R1.Pin_1
  N3: Bauteil1.D12/MISO, LED1.anode, LED3.anode
  N4: Bauteil1.D13/SCK, LED2.anode, LED4.anode
  N5: LED1.cathode, LED2.cathode, R2.Pin_0
  N6: LED3.cathode, LED4.cathode, R1.Pin_0
